// Logisim project 3_8decoder.circ as structural Verilog: 2 circuits, main circuit decoder_3to8
module decoder_3to8 (
  input  i0,
  input  i1,
  input  i3,
  output o0,
  output o1,
  output o2,
  output o3,
  output o4,
  output o5,
  output o6,
  output o7
);

  wire decoder_2to4_1_o0, decoder_2to4_1_o1, decoder_2to4_1_o2, decoder_2to4_1_o3, decoder_2to4_2_o0,
       decoder_2to4_2_o1, decoder_2to4_2_o2, decoder_2to4_2_o3, not_1_out;

  decoder_2to4 decoder_2to4_1 (
    .i0(i0), .i1(i1), .o0(decoder_2to4_1_o0), .o1(decoder_2to4_1_o1), .o2(decoder_2to4_1_o2),
    .o3(decoder_2to4_1_o3));
  decoder_2to4 decoder_2to4_2 (
    .i0(i0), .i1(i1), .o0(decoder_2to4_2_o0), .o1(decoder_2to4_2_o1), .o2(decoder_2to4_2_o2),
    .o3(decoder_2to4_2_o3));
  and and_1 (o0, decoder_2to4_1_o0, not_1_out);
  and and_2 (o1, decoder_2to4_1_o1, not_1_out);
  and and_3 (o2, decoder_2to4_1_o2, not_1_out);
  and and_4 (o3, decoder_2to4_1_o3, not_1_out);
  and and_5 (o4, decoder_2to4_2_o0, i3);
  and and_6 (o5, decoder_2to4_2_o1, i3);
  and and_7 (o6, decoder_2to4_2_o2, i3);
  and and_8 (o7, decoder_2to4_2_o3, i3);
  not not_1 (not_1_out, i3);
  // AND_Gate and_9 is placed but not wired
endmodule

module decoder_2to4 (
  input  i0,
  input  i1,
  output o0,
  output o1,
  output o2,
  output o3
);

  wire not_1_out, not_2_out;

  not not_1 (not_1_out, i0);
  not not_2 (not_2_out, i1);
  and and_1 (o0, not_1_out, not_2_out);
  and and_2 (o1, i0, not_2_out);
  and and_3 (o2, not_1_out, i1);
  and and_4 (o3, i0, i1);

  // Notes on the sheet:
  //   0
  //   0
  //   0
  //   1
  //   2
  //   3
endmodule
