// Logisim project 4bitscomparator.circ as structural Verilog: 1 circuit, main circuit comparator4bit
module comparator4bit (
  input  [3:0] a,
  input  [3:0] b,
  output equal
);

  wire not_1_out, not_2_out, not_3_out, not_4_out, xor_1_out, xor_2_out, xor_3_out, xor_4_out;

  xor xor_1 (xor_1_out, a[0], b[0]);
  xor xor_2 (xor_2_out, a[1], b[1]);
  xor xor_3 (xor_3_out, a[2], b[2]);
  xor xor_4 (xor_4_out, a[3], b[3]);
  not not_1 (not_1_out, xor_2_out);
  not not_2 (not_2_out, xor_1_out);
  not not_3 (not_3_out, xor_3_out);
  not not_4 (not_4_out, xor_4_out);
  and and_1 (equal, not_2_out, not_1_out, not_3_out, not_4_out);
  LED led_1 (.in(equal));
endmodule
