// Logisim project dflip_flop.circ as structural Verilog: 1 circuit, main circuit main
module main (
  input  d,
  input  reset,
  output q,
  output q_head
);

  wire clk_out, dlatch_1_q, not_1_out;

  Button clk (.out(clk_out));
  not not_1 (not_1_out, clk_out);
  dlatch dlatch_1 (.d(d), .we(not_1_out), .reset(reset), .q(dlatch_1_q));  // open: q_head
  dlatch dlatch_2 (.d(dlatch_1_q), .we(clk_out), .reset(reset), .q(q), .q_head(q_head));
endmodule
