// Logisim project dflipflop_en.circ as structural Verilog: 1 circuit, main circuit dflipflop_en
module dflipflop_en (
  input  d,
  input  clk,
  input  en,
  input  reset,
  output q,
  output q_head
);

  wire and_1_out;

  and and_1 (and_1_out, clk, en);
  dflip_flop dflip_flop_1 (.d(d), .clk(and_1_out), .reset(reset), .q(q), .q_head(q_head));
endmodule
