// Logisim project scpu.circ as structural Verilog: 8 circuits, main circuit main
module main (
  input  en,
  input  clk,
  input  reset
);

  wire and_1_out, and_2_out, comparator8bits_1_equal, not_1_out, opcode_o0, opcode_o2, opcode_o3, or_1_out;
  wire [1:0] mux1to2_2bit_1_o;
  wire [3:0] adder4bit_1_s, mux1to2_4bit_1_o, pc_q;
  wire [7:0] adder8bit_1_p4, gpr_1_rdata1, gpr_1_rdata2, mux1to2_8bit_1_o, rom8x8_1_op;

  mux1to2_4bit mux1to2_4bit_1 (.a(adder4bit_1_s), .b(rom8x8_1_op[5:2]), .sel(and_2_out), .o(mux1to2_4bit_1_o));
  reg4bit pc (.d(mux1to2_4bit_1_o), .en(en), .clk(clk), .reset(reset), .q(pc_q));
  adder4bit adder4bit_1 (.a(pc_q), .b(4'b0001), .cin(1'b0), .s(adder4bit_1_s));  // open: overflow, cout
  rom8x8 rom8x8_1 (.addr(pc_q), .op(rom8x8_1_op));
  decoder_2to4 opcode (
    .i0(rom8x8_1_op[6]), .i1(rom8x8_1_op[7]), .o0(opcode_o0), .o2(opcode_o2), .o3(opcode_o3));  // open: o1
  or or_1 (or_1_out, opcode_o0, opcode_o2);
  and and_1 (and_1_out, or_1_out, en);
  mux1to2_8bit mux1to2_8bit_1 (
    .a(adder8bit_1_p4), .b({4'b0000, rom8x8_1_op[3:0]}), .sel(rom8x8_1_op[7]), .o(mux1to2_8bit_1_o));
  mux1to2_2bit mux1to2_2bit_1 (.a(rom8x8_1_op[3:2]), .b(2'b00), .sel(rom8x8_1_op[6]), .o(mux1to2_2bit_1_o));
  gpr gpr_1 (
    .wdata(mux1to2_8bit_1_o), .waddr(rom8x8_1_op[5:4]), .wen(and_1_out), .clk(clk), .reset(reset),
    .raddr1(mux1to2_2bit_1_o), .raddr2(rom8x8_1_op[1:0]), .rdata1(gpr_1_rdata1), .rdata2(gpr_1_rdata2));
  // adder8bit adder8bit_1: pin names not known; wires that end beside it: gpr_1_rdata1, gpr_1_rdata2, 1'b0, adder8bit_1_p4
  comparator8bits comparator8bits_1 (.a(gpr_1_rdata1), .b(gpr_1_rdata2), .equal(comparator8bits_1_equal));
  not not_1 (not_1_out, comparator8bits_1_equal);
  and and_2 (and_2_out, not_1_out, opcode_o3);
endmodule

module rom8x8 (
  input  [3:0] addr,
  output [7:0] op
);

  wire and_1_out, and_2_out, and_3_out, and_4_out, and_5_out, and_6_out, and_7_out, and_8_out, and_9_out,
       and_10_out, and_11_out, and_12_out, and_13_out, and_14_out, and_15_out, and_16_out, and_17_out,
       and_18_out, and_19_out, and_20_out, and_21_out, and_22_out, and_23_out, and_24_out, and_25_out,
       and_26_out, and_27_out, and_28_out, and_29_out, and_30_out, and_31_out, and_32_out, and_33_out,
       and_34_out, and_35_out, and_36_out, and_37_out, and_38_out, and_39_out, and_40_out, and_41_out,
       and_42_out, and_43_out, and_44_out, and_45_out, and_46_out, and_47_out, and_48_out, and_49_out,
       and_50_out, and_51_out, and_52_out, and_53_out, and_54_out, and_55_out, and_56_out, and_57_out,
       and_58_out, and_59_out, and_60_out, and_61_out, and_62_out, and_63_out, and_64_out,
       decoder_4to16_1_o0, decoder_4to16_1_o1, decoder_4to16_1_o2, decoder_4to16_1_o3, decoder_4to16_1_o4,
       decoder_4to16_1_o5, decoder_4to16_1_o6, decoder_4to16_1_o7;

  decoder_4to16 decoder_4to16_1 (
    .i0(addr[0]), .i1(addr[1]), .i2(addr[2]), .i3(addr[3]), .o0(decoder_4to16_1_o0), .o1(decoder_4to16_1_o1),
    .o2(decoder_4to16_1_o2), .o3(decoder_4to16_1_o3), .o4(decoder_4to16_1_o4), .o5(decoder_4to16_1_o5),
    .o6(decoder_4to16_1_o6), .o7(decoder_4to16_1_o7));  // open: o8, o9, o10, o11, o12, o13, o14, o15
  and and_1 (and_1_out, decoder_4to16_1_o0, 1'b1);
  and and_2 (and_2_out, decoder_4to16_1_o1, 1'b1);
  and and_3 (and_3_out, decoder_4to16_1_o2, 1'b1);
  and and_4 (and_4_out, decoder_4to16_1_o3, 1'b1);
  and and_5 (and_5_out, decoder_4to16_1_o4, 1'b0);
  and and_6 (and_6_out, decoder_4to16_1_o5, 1'b0);
  and and_7 (and_7_out, decoder_4to16_1_o6, 1'b1);
  and and_8 (and_8_out, decoder_4to16_1_o7, 1'b1);
  or or_1 (op[7], and_1_out, and_2_out, and_3_out, and_4_out, and_5_out, and_6_out, and_7_out, and_8_out);
  and and_9 (and_9_out, decoder_4to16_1_o0, 1'b0);
  and and_10 (and_10_out, decoder_4to16_1_o1, 1'b0);
  and and_11 (and_11_out, decoder_4to16_1_o2, 1'b0);
  and and_12 (and_12_out, decoder_4to16_1_o3, 1'b0);
  and and_13 (and_13_out, decoder_4to16_1_o4, 1'b0);
  and and_14 (and_14_out, decoder_4to16_1_o5, 1'b0);
  and and_15 (and_15_out, decoder_4to16_1_o6, 1'b1);
  and and_16 (and_16_out, decoder_4to16_1_o7, 1'b1);
  or or_2 (op[6], and_9_out, and_10_out, and_11_out, and_12_out, and_13_out, and_14_out, and_15_out, and_16_out);
  and and_17 (and_17_out, decoder_4to16_1_o0, 1'b0);
  and and_18 (and_18_out, decoder_4to16_1_o1, 1'b0);
  and and_19 (and_19_out, decoder_4to16_1_o2, 1'b1);
  and and_20 (and_20_out, decoder_4to16_1_o3, 1'b1);
  and and_21 (and_21_out, decoder_4to16_1_o4, 1'b1);
  and and_22 (and_22_out, decoder_4to16_1_o5, 1'b0);
  and and_23 (and_23_out, decoder_4to16_1_o6, 1'b0);
  and and_24 (and_24_out, decoder_4to16_1_o7, 1'b0);
  or or_3 (op[5], and_17_out, and_18_out, and_19_out, and_20_out, and_21_out, and_22_out, and_23_out, and_24_out);
  and and_25 (and_25_out, decoder_4to16_1_o0, 1'b0);
  and and_26 (and_26_out, decoder_4to16_1_o1, 1'b1);
  and and_27 (and_27_out, decoder_4to16_1_o2, 1'b0);
  and and_28 (and_28_out, decoder_4to16_1_o3, 1'b1);
  and and_29 (and_29_out, decoder_4to16_1_o4, 1'b0);
  and and_30 (and_30_out, decoder_4to16_1_o5, 1'b1);
  and and_31 (and_31_out, decoder_4to16_1_o6, 1'b1);
  and and_32 (and_32_out, decoder_4to16_1_o7, 1'b1);
  or or_4 (op[4], and_25_out, and_26_out, and_27_out, and_28_out, and_29_out, and_30_out, and_31_out, and_32_out);
  and and_33 (and_33_out, decoder_4to16_1_o0, 1'b1);
  and and_34 (and_34_out, decoder_4to16_1_o1, 1'b0);
  and and_35 (and_35_out, decoder_4to16_1_o2, 1'b0);
  and and_36 (and_36_out, decoder_4to16_1_o3, 1'b0);
  and and_37 (and_37_out, decoder_4to16_1_o4, 1'b1);
  and and_38 (and_38_out, decoder_4to16_1_o5, 1'b0);
  and and_39 (and_39_out, decoder_4to16_1_o6, 1'b0);
  and and_40 (and_40_out, decoder_4to16_1_o7, 1'b1);
  or or_5 (op[3], and_33_out, and_34_out, and_35_out, and_36_out, and_37_out, and_38_out, and_39_out, and_40_out);
  and and_41 (and_41_out, decoder_4to16_1_o0, 1'b0);
  and and_42 (and_42_out, decoder_4to16_1_o1, 1'b0);
  and and_43 (and_43_out, decoder_4to16_1_o2, 1'b0);
  and and_44 (and_44_out, decoder_4to16_1_o3, 1'b0);
  and and_45 (and_45_out, decoder_4to16_1_o4, 1'b0);
  and and_46 (and_46_out, decoder_4to16_1_o5, 1'b1);
  and and_47 (and_47_out, decoder_4to16_1_o6, 1'b0);
  and and_48 (and_48_out, decoder_4to16_1_o7, 1'b1);
  or or_6 (op[2], and_41_out, and_42_out, and_43_out, and_44_out, and_45_out, and_46_out, and_47_out, and_48_out);
  and and_49 (and_49_out, decoder_4to16_1_o0, 1'b1);
  and and_50 (and_50_out, decoder_4to16_1_o1, 1'b0);
  and and_51 (and_51_out, decoder_4to16_1_o2, 1'b0);
  and and_52 (and_52_out, decoder_4to16_1_o3, 1'b1);
  and and_53 (and_53_out, decoder_4to16_1_o4, 1'b0);
  and and_54 (and_54_out, decoder_4to16_1_o5, 1'b1);
  and and_55 (and_55_out, decoder_4to16_1_o6, 1'b0);
  and and_56 (and_56_out, decoder_4to16_1_o7, 1'b1);
  or or_7 (op[1], and_49_out, and_50_out, and_51_out, and_52_out, and_53_out, and_54_out, and_55_out, and_56_out);
  and and_57 (and_57_out, decoder_4to16_1_o0, 1'b1);
  and and_58 (and_58_out, decoder_4to16_1_o1, 1'b1);
  and and_59 (and_59_out, decoder_4to16_1_o2, 1'b0);
  and and_60 (and_60_out, decoder_4to16_1_o3, 1'b0);
  and and_61 (and_61_out, decoder_4to16_1_o4, 1'b1);
  and and_62 (and_62_out, decoder_4to16_1_o5, 1'b1);
  and and_63 (and_63_out, decoder_4to16_1_o6, 1'b1);
  and and_64 (and_64_out, decoder_4to16_1_o7, 1'b1);
  or or_8 (op[0], and_57_out, and_58_out, and_59_out, and_60_out, and_61_out, and_62_out, and_63_out, and_64_out);
endmodule

module ram4x8 (
  input  [7:0] d,
  input  [1:0] addr,
  input  en,
  input  clk,
  input  reset,
  output [7:0] o
);

  wire and_1_out, and_2_out, and_3_out, and_4_out, decoder_2to4_1_o0, decoder_2to4_1_o1, decoder_2to4_1_o2,
       decoder_2to4_1_o3, ram0_0, ram0_1, ram0_2, ram0_3, ram0_4, ram0_5, ram0_6, ram0_7, ram1_0, ram1_1,
       ram1_2, ram1_3, ram1_4, ram1_5, ram1_6, ram1_7, ram2_0, ram2_1, ram2_2, ram2_3, ram2_4, ram2_5,
       ram2_6, ram2_7, ram3_0, ram3_1, ram3_2, ram3_3, ram3_4, ram3_5, ram3_6, ram3_7, undriven, undriven_2,
       undriven_3, undriven_4, undriven_5, undriven_6, undriven_7, undriven_8, undriven_9, undriven_10,
       undriven_11, undriven_12, undriven_13, undriven_14, undriven_15, undriven_16, undriven_17,
       undriven_18, undriven_19, undriven_20, undriven_21, undriven_22, undriven_23, undriven_24,
       undriven_25, undriven_26, undriven_27, undriven_28, undriven_29, undriven_30, undriven_31, undriven_32;

  or or_1 (o[0], ram0_0, ram1_0, ram2_0, ram3_0);
  or or_2 (o[1], ram0_1, ram1_1, ram2_1, ram3_1);
  or or_3 (o[2], ram0_2, ram1_2, ram2_2, ram3_2);
  or or_4 (o[3], ram0_3, ram1_3, ram2_3, ram3_3);
  or or_5 (o[4], ram0_4, ram1_4, ram2_4, ram3_4);
  or or_6 (o[5], ram0_5, ram1_5, ram2_5, ram3_5);
  or or_7 (o[6], ram0_6, ram1_6, ram2_6, ram3_6);
  or or_8 (o[7], ram0_7, ram1_7, ram2_7, ram3_7);
  decoder_2to4 decoder_2to4_1 (
    .i0(addr[0]), .i1(addr[1]), .o0(decoder_2to4_1_o0), .o1(decoder_2to4_1_o1), .o2(decoder_2to4_1_o2),
    .o3(decoder_2to4_1_o3));
  and and_1 (and_1_out, decoder_2to4_1_o0, en);
  and and_2 (and_2_out, decoder_2to4_1_o1, en);
  and and_3 (and_3_out, decoder_2to4_1_o2, en);
  and and_4 (and_4_out, decoder_2to4_1_o3, en);
  and and_5 (ram0_7, decoder_2to4_1_o0, undriven_2);
  and and_6 (ram1_7, decoder_2to4_1_o1, undriven_4);
  and and_7 (ram2_7, decoder_2to4_1_o2, undriven);
  and and_8 (ram3_7, decoder_2to4_1_o3, undriven_3);
  and and_9 (ram0_6, decoder_2to4_1_o0, undriven_6);
  and and_10 (ram1_6, decoder_2to4_1_o1, undriven_8);
  and and_11 (ram2_6, decoder_2to4_1_o2, undriven_5);
  and and_12 (ram3_6, decoder_2to4_1_o3, undriven_7);
  and and_13 (ram0_5, decoder_2to4_1_o0, undriven_10);
  and and_14 (ram1_5, decoder_2to4_1_o1, undriven_12);
  and and_15 (ram2_5, decoder_2to4_1_o2, undriven_9);
  and and_16 (ram3_5, decoder_2to4_1_o3, undriven_11);
  and and_17 (ram0_4, decoder_2to4_1_o0, undriven_14);
  and and_18 (ram1_4, decoder_2to4_1_o1, undriven_16);
  and and_19 (ram2_4, decoder_2to4_1_o2, undriven_13);
  and and_20 (ram3_4, decoder_2to4_1_o3, undriven_15);
  and and_21 (ram0_3, decoder_2to4_1_o0, undriven_18);
  and and_22 (ram1_3, decoder_2to4_1_o1, undriven_20);
  and and_23 (ram2_3, decoder_2to4_1_o2, undriven_17);
  and and_24 (ram3_3, decoder_2to4_1_o3, undriven_19);
  and and_25 (ram0_2, decoder_2to4_1_o0, undriven_22);
  and and_26 (ram1_2, decoder_2to4_1_o1, undriven_24);
  and and_27 (ram2_2, decoder_2to4_1_o2, undriven_21);
  and and_28 (ram3_2, decoder_2to4_1_o3, undriven_23);
  and and_29 (ram0_1, decoder_2to4_1_o0, undriven_26);
  and and_30 (ram1_1, decoder_2to4_1_o1, undriven_28);
  and and_31 (ram2_1, decoder_2to4_1_o2, undriven_25);
  and and_32 (ram3_1, decoder_2to4_1_o3, undriven_27);
  and and_33 (ram0_0, decoder_2to4_1_o0, undriven_30);
  and and_34 (ram1_0, decoder_2to4_1_o1, undriven_32);
  and and_35 (ram2_0, decoder_2to4_1_o2, undriven_29);
  and and_36 (ram3_0, decoder_2to4_1_o3, undriven_31);
endmodule

module gpr (
  input  [7:0] wdata,
  input  [1:0] waddr,
  input  wen,
  input  clk,
  input  reset,
  input  [1:0] raddr1,
  input  [1:0] raddr2,
  output [7:0] rdata1,
  output [7:0] rdata2
);

  wire and_1_out, and_2_out, and_3_out, and_4_out, decoder_2to4_1_o0, decoder_2to4_1_o1, decoder_2to4_1_o2,
       decoder_2to4_1_o3;
  wire [7:0] and_5_out, and_6_out, and_7_out, and_8_out, and_9_out, and_10_out, and_11_out, and_12_out, ram0,
       ram1, ram2, ram3;
  wire [7:7] decoder_2to4_2_o0, decoder_2to4_2_o1, decoder_2to4_2_o2, decoder_2to4_2_o3, decoder_2to4_3_o0,
       decoder_2to4_3_o1, decoder_2to4_3_o2, decoder_2to4_3_o3;

  decoder_2to4 decoder_2to4_1 (
    .i0(waddr[0]), .i1(waddr[1]), .o0(decoder_2to4_1_o0), .o1(decoder_2to4_1_o1), .o2(decoder_2to4_1_o2),
    .o3(decoder_2to4_1_o3));
  decoder_2to4 decoder_2to4_2 (
    .i0(raddr1[0]), .i1(raddr1[1]), .o0(decoder_2to4_2_o0[7]), .o1(decoder_2to4_2_o1[7]),
    .o2(decoder_2to4_2_o2[7]), .o3(decoder_2to4_2_o3[7]));
  decoder_2to4 decoder_2to4_3 (
    .i0(raddr2[0]), .i1(raddr2[1]), .o0(decoder_2to4_3_o0[7]), .o1(decoder_2to4_3_o1[7]),
    .o2(decoder_2to4_3_o2[7]), .o3(decoder_2to4_3_o3[7]));
  and and_1 (and_1_out, decoder_2to4_1_o0, wen);
  and and_2 (and_2_out, decoder_2to4_1_o1, wen);
  and and_3 (and_3_out, decoder_2to4_1_o2, wen);
  and and_4 (and_4_out, decoder_2to4_1_o3, wen);
  assign and_5_out = {8{decoder_2to4_2_o0[7]}} & ram0;  // AND_Gate and_5, 8 bits wide
  assign and_6_out = {8{decoder_2to4_2_o1[7]}} & ram1;  // AND_Gate and_6, 8 bits wide
  assign and_7_out = {8{decoder_2to4_2_o2[7]}} & ram2;  // AND_Gate and_7, 8 bits wide
  assign and_8_out = {8{decoder_2to4_2_o3[7]}} & ram3;  // AND_Gate and_8, 8 bits wide
  assign and_9_out = {8{decoder_2to4_3_o0[7]}} & ram0;  // AND_Gate and_9, 8 bits wide
  assign and_10_out = {8{decoder_2to4_3_o1[7]}} & ram1;  // AND_Gate and_10, 8 bits wide
  assign and_11_out = {8{decoder_2to4_3_o2[7]}} & ram2;  // AND_Gate and_11, 8 bits wide
  assign and_12_out = {8{decoder_2to4_3_o3[7]}} & ram3;  // AND_Gate and_12, 8 bits wide
  dflipflop_en_8bit dflipflop_en_8bit_1 (
    .d(wdata), .clk(clk), .en(and_1_out), .reset(reset), .q(ram0));  // open: q_head
  dflipflop_en_8bit dflipflop_en_8bit_2 (
    .d(wdata), .clk(clk), .en(and_2_out), .reset(reset), .q(ram1));  // open: q_head
  dflipflop_en_8bit dflipflop_en_8bit_3 (
    .d(wdata), .clk(clk), .en(and_3_out), .reset(reset), .q(ram2));  // open: q_head
  dflipflop_en_8bit dflipflop_en_8bit_4 (
    .d(wdata), .clk(clk), .en(and_4_out), .reset(reset), .q(ram3));  // open: q_head
  assign rdata1 = and_5_out | and_6_out | and_7_out | and_8_out;  // OR_Gate or_1, 8 bits wide
  assign rdata2 = and_9_out | and_10_out | and_11_out | and_12_out;  // OR_Gate or_2, 8 bits wide
endmodule

module mux1to2_8bit (
  input  [7:0] a,
  input  [7:0] b,
  input  sel,
  output [7:0] o
);

  wire [7:0] and_1_out, and_2_out;
  wire [7:7] not_1_out;

  not not_1 (not_1_out[7], sel);
  assign and_1_out = a & {8{not_1_out[7]}};  // AND_Gate and_1, 8 bits wide
  assign and_2_out = b & {8{sel}};  // AND_Gate and_2, 8 bits wide
  assign o = and_1_out | and_2_out;  // OR_Gate or_1, 8 bits wide
endmodule

module comparator8bits (
  input  [7:0] a,
  input  [7:0] b,
  output equal
);

  wire [7:0] not_1_out, xor_1_out;

  assign xor_1_out = a ^ b;  // XOR_Gate xor_1, 8 bits wide
  assign not_1_out = ~xor_1_out;  // NOT_Gate not_1, 8 bits wide
  and and_1 (equal, not_1_out[0], not_1_out[1], not_1_out[2], not_1_out[3], not_1_out[4], not_1_out[5], not_1_out[6], not_1_out[7]);
  LED led_1 (.in(equal));
endmodule

module mux1to2_2bit (
  input  [1:0] a,
  input  [1:0] b,
  input  sel,
  output [1:0] o
);

  wire [1:0] and_1_out, and_2_out;
  wire [1:1] not_1_out;

  not not_1 (not_1_out[1], sel);
  assign and_1_out = a & {2{not_1_out[1]}};  // AND_Gate and_1, 2 bits wide
  assign and_2_out = b & {2{sel}};  // AND_Gate and_2, 2 bits wide
  assign o = and_1_out | and_2_out;  // OR_Gate or_1, 2 bits wide
endmodule

module mux1to2_4bit (
  input  [3:0] a,
  input  [3:0] b,
  input  sel,
  output [3:0] o
);

  wire [3:0] and_1_out, and_2_out;
  wire [3:3] not_1_out;

  not not_1 (not_1_out[3], sel);
  assign and_1_out = a & {4{not_1_out[3]}};  // AND_Gate and_1, 4 bits wide
  assign and_2_out = b & {4{sel}};  // AND_Gate and_2, 4 bits wide
  assign o = and_1_out | and_2_out;  // OR_Gate or_1, 4 bits wide
endmodule
